// Digital circuit encoder.dig as structural Verilog
module encoder (
  input  clk,
  input  canalA,
  input  canalB,
  output giroPositivo,
  output giroNegativo
);

  wire and_1_out, and_2_out, and_3_out, and_4_out, d_ff_1_q, d_ff_2_q, d_ff_3_q, d_ff_4_q, d_ff_5_q,
       d_ff_6_q, d_ff_7_nq, jk_ff_1_q, or_1_out, or_2_out, xor_1_out, xor_2_out, xor_3_out;

  D_FF d_ff_1 (.D(canalA), .C(clk), .Q(d_ff_1_q));  // open: nQ
  D_FF d_ff_2 (.D(canalB), .C(clk), .Q(d_ff_2_q));  // open: nQ
  xor xor_1 (xor_1_out, canalA, d_ff_1_q);
  xor xor_2 (xor_2_out, canalA, canalB);
  xor xor_3 (xor_3_out, canalB, d_ff_2_q);
  and and_1 (and_1_out, xor_1_out, xor_2_out);
  and and_2 (and_2_out, xor_2_out, xor_3_out);
  or or_1 (or_1_out, xor_1_out, xor_3_out);
  JK_FF jk_ff_1 (.J(and_1_out), .C(clk), .K(and_2_out), .Q(jk_ff_1_q));  // open: nQ
  D_FF d_ff_3 (.D(xor_1_out), .C(or_1_out), .Q(d_ff_3_q));  // open: nQ
  D_FF d_ff_4 (.D(xor_3_out), .C(or_1_out), .Q(d_ff_4_q));  // open: nQ
  D_FF d_ff_5 (.D(d_ff_3_q), .C(or_1_out), .Q(d_ff_5_q));  // open: nQ
  D_FF d_ff_6 (.D(d_ff_4_q), .C(or_1_out), .Q(d_ff_6_q));  // open: nQ
  and and_3 (and_3_out, d_ff_3_q, d_ff_5_q);
  and and_4 (and_4_out, d_ff_4_q, d_ff_6_q);
  or or_2 (or_2_out, and_3_out, and_4_out);
  D_FF d_ff_7 (.D(jk_ff_1_q), .C(or_2_out), .nQ(d_ff_7_nq));  // open: Q
  Demultiplexer demultiplexer_1 (.sel(d_ff_7_nq), .in(or_1_out), .out_0(giroNegativo), .out_1(giroPositivo));

  // Notes on the sheet:
  //   clk: Hz: 10
  //   AP
  //   BP
  //   dirRotacionCe
  //   resetDireccion
endmodule
