// Digital circuit romContador.dig as structural Verilog
module romContador (
  input  clk,
  input  sw,
  output [15:0] data
);

  wire [5:0] counter_1_out;

  Counter #(.Bits(6)) counter_1 (.en(1'b1), .C(clk), .clr(~sw), .out(counter_1_out));  // open: ovf
  ROM #(.AddrBits(6), .Bits(16)) rom (.A(counter_1_out), .sel(sw), .D(data));

  // Notes on the sheet:
  //   clk: Hz: 2
  //   contents of rom (hex, n*v repeats v):
  //   106,115,126,137,14a,15d,172,188,19f,1b8,1d2,1ee,0,106,115,126
  //   ,120,1ec,106,115,126,137,14a,15d,1b8,19f,1b8,1d2,1ee,0,106,115
  //   ,106,106,115,126,137,14a,15d,172,1b8,19f,1b8,1d2,1ee,0,106,115
  //   ,18,8,19f,1b8,1d2,1ee,0,106,531*0,104,16773705*0,34,18*0,25,35*0
  //   ,954,136*0,25,15*0,2552a,549*0,25,298*0,1158a5,288*0,4365,272*0
  //   ,4355,368*0,218aa,239*0,21955,143*0,86b,176*0,6e,29*0,112,18*0
  //   ,25,72*0,23,0,2c,13*0,25,5*0,25,17*0,3,7*0,4,16*0,25,17*0,2c,0,0,0
  //   ,25,10*0,4,5*0,8,5*0,2c,8*0,1c,4*0,2c,56*0,1c,11*0,2c,7*0,4,49*0,24
endmodule
