// Digital circuit L2ANALISIS.dig as structural Verilog
module L2ANALISIS (
  input  I1_Red_Electrica,
  input  I3_Paro_Emergencia,
  input  I4_Energia_Solar,
  output Q8_Energia_Casa,
  output Q1a_Tipo_de_Red_RE,
  output Q2_I_Red_ELectrica,
  output Q1b_TIpo_de_Red_B,
  output Q3_I_Bateria,
  output Q4_I_Energia_Solar,
  output Q5_I_Paro_Emergencia
);

  wire and_2_out, and_3_out, or_1_out;

  D_FF d_ff_1 (.D(1'b1), .C(I4_Energia_Solar), .Q(Q3_I_Bateria));  // open: nQ
  and and_1 (Q1b_TIpo_de_Red_B, ~I1_Red_Electrica, Q3_I_Bateria);  // And
  not not_1 (Q1a_Tipo_de_Red_RE, Q1b_TIpo_de_Red_B);
  and and_2 (and_2_out, I1_Red_Electrica, ~Q1b_TIpo_de_Red_B);  // And
  and and_3 (and_3_out, Q1b_TIpo_de_Red_B, Q3_I_Bateria);
  and and_4 (Q8_Energia_Casa, or_1_out, ~I3_Paro_Emergencia);  // And
  or or_1 (or_1_out, and_2_out, and_3_out);

  assign Q2_I_Red_ELectrica = I1_Red_Electrica;
  assign Q4_I_Energia_Solar = I4_Energia_Solar;
  assign Q5_I_Paro_Emergencia = I3_Paro_Emergencia;

  // Notes on the sheet:
  //   I1_Red_Electrica: i+
  //   I2. Bateria
  //   Q6. Rele Conmutador
  //   Q7. Rele Energizador
endmodule
